# Fritzing sketch auto_splash_catapult (saved by Fritzing 0.9.2b)
breadboards: 1

parts:
  元件1 = Arduino Uno (Rev3) - ICSP
  VCC1 = 4 x AAA Battery Mount
  VCC2 = 4 x AAA Battery Mount
  J3 = Basic Servo
  J4 = Basic Servo
  S2 = Round Pushbutton
  R1 = Resistor [tolerance=±5% resistance=15k package="0603 [SMD]"]

nets:
  N1: 元件1.D9_PWM, J3.pulse
  N2: 元件1.D2, S2.leg0, R1.Pin_1
  N3: 元件1.D6_PWM, J4.pulse
  N4: 元件1.5V, S2.leg1
  GND: 元件1.GND, VCC1.-, VCC2.-, J3.gnd, R1.Pin_0
  N5: VCC1.+, J4.vcc
  N6: VCC2.+, J3.vcc

notes:
  360
  180
